# Fritzing sketch sensors (saved by Fritzing 0.9.2b)

parts:
  GPS1 = Adafruit Ultimate GPS Breakout
  IMU1 = Adafruit 10-DOF IMU Breakout
  Part1 = XBee Explorer Regulated
  U2 = LIPO-110mAh [package=lipo-110]  # not connected
  U3 = XBEE-1 [package=xbee-1]  # not connected
  Part2 = Adafruit Feather M0 Adalogger [part_number="Adafruit #2796"]
  JP1 = Header 3 [package=screwterminal-3.5mm-3_lock.007s]

nets:
  N1: GPS1.TX, Part2.D11
  N2: GPS1.RX, Part2.D10
  GND: GPS1.GND, IMU1.GND, Part1.GND, Part2.GND, JP1.2
  VIN: GPS1.VIN, IMU1.VIN, Part1.5V, Part2.+3V3
  N3: IMU1.SCL, Part2.SCL
  N4: IMU1.SDA, Part2.SDA
  N5: Part1.DIN, Part2.D0
  N6: Part1.DOUT, Part2.D1
  N7: Part2.D6, JP1.1
  N8: Part2.D5, JP1.3

custom parts:
  Adafruit Feather M0 Adalogger: This is the Adafruit Feather M0 Adalogger - our take on an 'all-in-one' Cortex M0 datalogger (or data-reader) with built in USB and battery charging. Its an Adafruit Feather M0 with a microSD holder ready to rock! We have other boards in the Feather family, check'em out here At the Feather M0's heart is an ATSAMD21G18 ARM Cortex M0 processor, clocked at 48 MHz and at 3.3V logic, the same one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
