# Fritzing sketch wiring (saved by Fritzing 0.9.2b)

parts:
  Adafruit_Atmega32u1 = Adafruit Atmega32u4 Breakout Board [part_number="Atmega 32u4"]
  GPS1 = Adafruit Ultimate GPS Breakout
  IMU1 = Adafruit 10-DOF IMU Breakout
  Part1 = XBee Explorer Regulated
  U2 = LIPO-110mAh [package=lipo-110]
  U3 = XBEE-1 [package=xbee-1]  # not connected

nets:
  N1: Adafruit_Atmega32u1.C7, GPS1.TX
  N2: Adafruit_Atmega32u1.C6, GPS1.RX
  N3: Adafruit_Atmega32u1.B5, IMU1.SCL
  N4: Adafruit_Atmega32u1.B4, IMU1.SDA
  N5: Adafruit_Atmega32u1.GND#14, U2.-
  N6: Adafruit_Atmega32u1.VCC, U2.+
  VIN: Adafruit_Atmega32u1.3V, GPS1.VIN, IMU1.VIN, Part1.5V
  N7: Adafruit_Atmega32u1.D6, Part1.DIN
  N8: Adafruit_Atmega32u1.D7, Part1.DOUT
  GND: Adafruit_Atmega32u1.GND#36, GPS1.GND, IMU1.GND, Part1.GND
